# Fritzing sketch CySump (saved by Fritzing 0.9.3b)
circuit board: 12.2109cm x 9.21139cm
breadboards: 2

parts:
  Adafruit_HUZZAH_ESP8266 = Adafruit HUZZAH ESP8266 Breakout [part_number=2471]
  Power_Relay_Featherwing = Adafruit PowerRelay Feather Wing [part_number="Adafruit #3191"]
  LED2 = LED - 5mm [color="Red (633nm)" package="5 mm [THT]"]
  LED1 = LED - 5mm [color="Green (570nm)" package="5 mm [THT]"]
  LED3 = LED - 5mm [color="Yellow (595nm)" package="5 mm [THT]"]
  J1 = Piezo Speaker
  J2 = Screw terminal - 2 pins [package=THT]
  HC-SR04_Sensor = HC-SR04 Ultrasonic Distance Sensor
  S1 = SPST Switch [package=switche-dpdt]

nets:
  GND: Adafruit_HUZZAH_ESP8266.GND, Power_Relay_Featherwing.GND, LED2.cathode, LED1.cathode, LED3.cathode, J1.pin1, J2.pin1, HC-SR04_Sensor.GND
  N1: Adafruit_HUZZAH_ESP8266.V+, S1.O
  N2: Adafruit_HUZZAH_ESP8266.#12, HC-SR04_Sensor.TRIG
  N3: Adafruit_HUZZAH_ESP8266.#14, HC-SR04_Sensor.ECHO
  N4: Adafruit_HUZZAH_ESP8266.#16, J1.pin2
  N5: Adafruit_HUZZAH_ESP8266.#5, LED3.anode
  N6: Adafruit_HUZZAH_ESP8266.#4, LED2.anode
  N7: Adafruit_HUZZAH_ESP8266.#2, LED1.anode
  N8: Adafruit_HUZZAH_ESP8266.#15, Power_Relay_Featherwing.A
  3.3V: Adafruit_HUZZAH_ESP8266.3V, Power_Relay_Featherwing.3.3V, HC-SR04_Sensor.VCC
  N9: J2.pin2, S1.P

notes:
  CySump Board Rev 1.0
  WiFi Act
  Alarm
  Pump
  CySump, Automated IoT Sump Pump Controller, 1.0
  Note: HC-SR04 Schematic is incorrect.  GND and ECHO pins are swapped.

custom parts:
  Adafruit PowerRelay Feather Wing: A Feather board without ambition is a Feather board without FeatherWings! This is the Power Relay FeatherWing. It gives you power to control, and control over power. Put simply, you can now turn on and off lamps, fans, solenoids, and other small appliances that run on up to 250VAC or DC power using any Feather board. Compared to our smaller Relay FeatherWings, this one can handle a beefy 1200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
